# Fritzing sketch printplaatRaspberry (saved by Fritzing 0.9.3b)
circuit board: 6.04455cm x 4.62293cm

parts:
  Raspberry_Pi_1 = Raspberry Pi 3 [part_number=RPI-3-V1.2]
  S1 = SWITCH-MOMENTARY-2 [package=tactile-pth]
  S2 = SWITCH-MOMENTARY-2 [package=tactile-pth]
  S3 = SWITCH-MOMENTARY-2 [package=tactile-pth]
  KY-1 = Keyes Relay [package=THT]
  KY-2 = Keyes Relay [package=THT]  # not connected
  KY-3 = Keyes Relay [package=THT]
  KY-4 = Keyes Relay [package=THT]
  LED1 = smd LED [color="Red (633nm)" package="0603 [SMD]"]
  LED2 = smd LED [color="Red (633nm)" package="0603 [SMD]"]
  LED3 = smd LED [color="Red (633nm)" package="0603 [SMD]"]

nets:
  3V3: Raspberry_Pi_1.3v3, Raspberry_Pi_1.3V3, KY-1.power
  N1: Raspberry_Pi_1.GPIO4, KY-1.signal
  N2: Raspberry_Pi_1.GND, Raspberry_Pi_1.GPIO14, KY-1.ground
  N3: Raspberry_Pi_1.GPIO17, KY-3.signal
  N4: Raspberry_Pi_1.GPIO27, KY-4.signal
  N5: Raspberry_Pi_1.GPIO22, S1.2
  N6: Raspberry_Pi_1.GPIO10, S2.2
  N7: Raspberry_Pi_1.GPIO9, S3.2
  N8: S1.1, S2.1
  N9: KY-1.NO, LED1.anode
  N10: KY-3.NO, LED2.anode
  N11: KY-4.NO, LED3.anode

notes:
  9-12V Power Supply

custom parts:
  Keyes Relay: The Keyes 5V relay module is suitable for SCM development, home appliance control. It uses a 5V~12V TIL control signal which can control DC / AC signal.
